# Fritzing sketch spi-connection (saved by Fritzing 0.9.3b)
breadboards: 1

parts:
  U1 = 74HC595 SMD [package="SO16 [SMD]"]
  U2 = 74HC595 SMD [package="SO16 [SMD]"]
  U3 = 74HC595 SMD [package="SO16 [SMD]"]
  U4 = 74HC595 SMD [package="SO16 [SMD]"]
  J1 = female pin header, 8 pins [form="♀ (female)"]
  J2 = female pin header, 8 pins [form="♀ (female)"]
  J3 = female pin header, 8 pins [form="♀ (female)"]
  J4 = female pin header, 8 pins [form="♀ (female)"]

nets:
  N1: U1.Q1, J1.pin2
  N2: U1.Q2, J1.pin3
  N3: U1.Q3, J1.pin4
  N4: U1.Q4, J1.pin5
  N5: U1.Q5, J1.pin6
  N6: U1.Q6, J1.pin7
  N7: U1.Q7, J1.pin8
  GND: U1.GND, U1.OE, U2.GND, U2.OE, U3.GND, U3.OE, U4.GND, U4.OE
  5V: U1.MR, U1.VCC, U2.MR, U2.VCC, U3.MR, U3.VCC, U4.MR, U4.VCC
  SCLK: U1.SH_CP, U2.SH_CP, U3.SH_CP, U4.SH_CP
  RCLK: U1.ST_CP, U2.ST_CP, U3.ST_CP, U4.ST_CP
  N8: U1.DS, U2.Q7'
  N9: U1.Q0, J1.pin1
  N10: U2.Q1, J2.pin2
  N11: U2.Q2, J2.pin3
  N12: U2.Q3, J2.pin4
  N13: U2.Q4, J2.pin5
  N14: U2.Q5, J2.pin6
  N15: U2.Q6, J2.pin7
  N16: U2.Q7, J2.pin8
  N17: U2.DS, U3.Q7'
  N18: U2.Q0, J2.pin1
  N19: U3.Q1, J3.pin2
  N20: U3.Q2, J3.pin3
  N21: U3.Q3, J3.pin4
  N22: U3.Q4, J3.pin5
  N23: U3.Q5, J3.pin6
  N24: U3.Q6, J3.pin7
  N25: U3.Q7, J3.pin8
  N26: U3.DS, U4.Q7'
  N27: U3.Q0, J3.pin1
  N28: U4.Q1, J4.pin2
  N29: U4.Q2, J4.pin3
  N30: U4.Q3, J4.pin4
  N31: U4.Q4, J4.pin5
  N32: U4.Q5, J4.pin6
  N33: U4.Q6, J4.pin7
  N34: U4.Q7, J4.pin8
  DATA: U4.DS
  N35: U4.Q0, J4.pin1

notes:
  DATA = GPIO13 = D7 (NodeMCU/WemosD1) = MOSI
  RCLK = GPIO15 = D8 (NodeMCU/WemosD1) = CS
  SCLK = GPIO14 = D5 (NodeMCU/WemosD1) = CLK
